# Fritzing sketch hodor_rfid (saved by Fritzing 0.9.3b)
breadboards: 1

parts:
  Part1 = Arduino Pro Mini (3.3V)
  Part2 = FTDI Basic Programmer
  J2 = Power Jack [package=power_jack_pth]
  Weigand_RFID = Header 4 [package=screwterminal-3.5mm-4_lock]
  R1 = Resistor [tolerance=±5% resistance=20k package=THT]
  R2 = Resistor [tolerance=±5% resistance=47k package=THT]
  R3 = Resistor [tolerance=±5% resistance=20k package=THT]
  R4 = Resistor [tolerance=±5% resistance=47k package=THT]
  OMRON1 = OMRON PCB Power Relay – G5LE [part_number="G5LE-1\n" package=THT]
  D1 = Diode [package=diode-1n4148]
  Q1 = NPN-Transistor [package="TO92 [THT]"]
  R5 = Resistor [tolerance=±5% resistance=1k package=THT]
  J3 = female pin header, 2 pins [form="♀ (female)"]

nets:
  N1: Part1.DTR, Part2.DTR
  N2: Part1.TXO, Part2.RXI
  N3: Part1.RXI, Part2.TXO
  GND: Part1.GND, Part2.GND, J2.GND, Weigand_RFID.1, R2.Pin_0, R4.Pin_0, OMRON1.C, Q1.B
  N4: J2.PWR, Weigand_RFID.4, J3.pin1
  N5: Weigand_RFID.2, R3.Pin_0
  N6: Weigand_RFID.3, R1.Pin_0
  N7: R1.Pin_1, R2.Pin_1
  N8: R3.Pin_1, R4.Pin_1
  N9: OMRON1.COIL1, D1.C
  N10: OMRON1.COIL2, D1.A, Q1.E
  N11: OMRON1.B, J3.pin2
  N12: Q1.C, R5.Pin_1

notes:
  RFID (Weigand)
  Data0 - Green
  Data1 - White
  Door
  Strike
